# Fritzing sketch potentiometer (saved by Fritzing 0.8.7b)
breadboards: 1

parts:
  Part1 = Arduino Uno (Rev3)
  U1 = POT [package=alps_pot]
  LED1 = LED - 5mm [color="Red (633nm)" package="5 mm [THT]"]
  R1 = Resistor [tolerance=±5% resistance=220 package=THT]

nets:
  N1: Part1.A0, U1.S
  N2: Part1.D9_PWM, LED1.cathode
  N3: Part1.GND, U1.A, R1.Pin_1
  N4: Part1.5V, U1.E
  N5: LED1.anode, R1.Pin_0
