# Fritzing sketch pushbutton-pulldown (saved by Fritzing 0.8.7b)
breadboards: 1

parts:
  Part1 = Arduino Uno (Rev3)
  S1 = Pushbutton [package="[THT]"]
  R1 = Resistor [tolerance=±5% resistance=10k package=THT]

nets:
  N1: Part1.D2, S1.Pin_1, S1.Pin_2, R1.Pin_0
  N2: Part1.5V, S1.Pin_3, S1.Pin_4
  N3: Part1.GND, R1.Pin_1
